# Fritzing sketch 连线图 (saved by Fritzing 0.9.3b)
breadboards: 1

parts:
  元件1 = Arduino Pro Mini v13
  J1 = Basic Servo
  J2 = Basic Servo
  J3 = Basic Servo
  J4 = Basic Servo
  hc-sr1 = hc-sr04
  hc-sr2 = hc-sr04
  hc-sr3 = hc-sr04
  VCC1 = Battery
  U1 = SWITCH_SPDT [package=kps-1290]
  J5 = Basic Servo

nets:
  VCC: 元件1.VCC, J1.vcc, J2.vcc, J3.vcc, J4.vcc, hc-sr1.VCC, hc-sr2.VCC, hc-sr3.VCC, U1.P, J5.vcc
  GND: 元件1.GND, J1.gnd, J2.gnd, J3.gnd, J4.gnd, hc-sr1.GND, hc-sr2.GND, hc-sr3.GND, VCC1.-, J5.gnd
  N1: 元件1.D13/SCK, hc-sr2.Trig
  N2: 元件1.D12/MISO, hc-sr2.Echo
  N3: 元件1.D11_PWM/MOSI, hc-sr3.Trig
  N4: 元件1.D10_PWM/SS, hc-sr3.Echo
  N5: 元件1.D8, hc-sr1.Echo
  N6: 元件1.D7, hc-sr1.Trig
  N7: 元件1.D6_PWM, J2.pulse
  N8: 元件1.D5_PWM, J3.pulse
  N9: 元件1.D4, J4.pulse
  N10: 元件1.D3_PWM, J5.pulse
  N11: 元件1.D2, J1.pulse
  N12: VCC1.+, U1.O
